# Fritzing sketch NovoPainel (saved by Fritzing 0.9.2b)
circuit board: 17.3cm x 7cm
breadboards: 1

parts:
  J3 = female pin header, 2 pins [form="♀ (female)"]
  C2 = Electrolytic Capacitor [capacitance=100nF package="200 mil [THT, electrolytic]"]
  U1 = Voltage Regulator [package=to220-adj]
  C3 = Electrolytic Capacitor [capacitance=1µF package="200 mil [THT, electrolytic]"]
  J5 = female pin header, 2 pins [form="♀ (female)"]
  J6 = Screw terminal - 2 pins [package=THT]
  J7 = Screw terminal - 2 pins [package=THT]
  J8 = female pin header, 2 pins [form="♀ (female)"]
  J9 = female pin header, 2 pins [form="♀ (female)"]
  J10 = Screw terminal - 2 pins [package=THT]
  C4 = Electrolytic Capacitor [capacitance=0.22mF package="200 mil [THT, electrolytic]"]
  R3 = Resistor [tolerance=±5% resistance=330 package=THT]
  J12 = female pin header, 2 pins [form="♀ (female)"]
  J13 = female pin header, 2 pins [form="♀ (female)"]
  R4 = Resistor [tolerance=±5% resistance=330 package=THT]
  C5 = Electrolytic Capacitor [capacitance=0.22mF package="200 mil [THT, electrolytic]"]
  J15 = female pin header, 2 pins [form="♀ (female)"]
  R1 = Resistor [tolerance=±5% resistance=220 package=THT]
  U2 = POT [package=3362u]
  J14 = female pin header, 2 pins [form="♀ (female)"]
  J16 = female pin header, 2 pins [form="♀ (female)"]
  R5 = Resistor [tolerance=±5% resistance=220 package=THT]
  J17 = female pin header, 2 pins [form="♀ (female)"]
  J18 = female pin header, 2 pins [form="♀ (female)"]
  R6 = Resistor [tolerance=±5% resistance=220 package=THT]
  J19 = female pin header, 2 pins [form="♀ (female)"]
  J20 = female pin header, 2 pins [form="♀ (female)"]
  J21 = female pin header, 2 pins [form="♀ (female)"]
  R7 = Resistor [tolerance=±5% resistance=220 package=THT]
  J22 = female pin header, 2 pins [form="♀ (female)"]
  J23 = female pin header, 2 pins [form="♀ (female)"]
  J24 = female pin header, 2 pins [form="♀ (female)"]
  R8 = Resistor [tolerance=±5% resistance=220 package=THT]
  J25 = female pin header, 2 pins [form="♀ (female)"]
  J26 = female pin header, 2 pins [form="♀ (female)"]
  J27 = female pin header, 2 pins [form="♀ (female)"]
  R9 = Resistor [tolerance=±5% resistance=220 package=THT]
  J28 = female pin header, 2 pins [form="♀ (female)"]
  J29 = female pin header, 2 pins [form="♀ (female)"]
  J30 = female pin header, 2 pins [form="♀ (female)"]
  R10 = Resistor [tolerance=±5% resistance=220 package=THT]
  J31 = female pin header, 2 pins [form="♀ (female)"]
  J32 = female pin header, 2 pins [form="♀ (female)"]
  J33 = female pin header, 2 pins [form="♀ (female)"]
  R11 = Resistor [tolerance=±5% resistance=220 package=THT]
  J34 = female pin header, 2 pins [form="♀ (female)"]
  J35 = female pin header, 2 pins [form="♀ (female)"]
  J36 = female pin header, 2 pins [form="♀ (female)"]
  R12 = Resistor [tolerance=±5% resistance=220 package=THT]
  J37 = female pin header, 2 pins [form="♀ (female)"]
  J38 = female pin header, 2 pins [form="♀ (female)"]
  J39 = female pin header, 2 pins [form="♀ (female)"]
  J40 = female pin header, 2 pins [form="♀ (female)"]
  J41 = female pin header, 2 pins [form="♀ (female)"]
  R13 = Resistor [tolerance=±5% resistance=220 package=THT]
  J42 = female pin header, 2 pins [form="♀ (female)"]
  J43 = female pin header, 2 pins [form="♀ (female)"]
  J44 = female pin header, 2 pins [form="♀ (female)"]
  R14 = Resistor [tolerance=±5% resistance=220 package=THT]
  J45 = female pin header, 2 pins [form="♀ (female)"]
  J46 = female pin header, 2 pins [form="♀ (female)"]
  J47 = female pin header, 2 pins [form="♀ (female)"]
  C6 = Electrolytic Capacitor [capacitance=0.22mF package="200 mil [THT, electrolytic]"]
  C7 = Electrolytic Capacitor [capacitance=100nF package="100 mil [THT, electrolytic]"]
  R15 = Resistor [tolerance=±5% resistance=100 package=THT]
  R16 = Resistor [tolerance=±5% resistance=330 package=THT]
  J48 = female pin header, 2 pins [form="♀ (female)"]
  J49 = female pin header, 2 pins [form="♀ (female)"]
  J50 = female pin header, 2 pins [form="♀ (female)"]
  C8 = Electrolytic Capacitor [capacitance=0.22mF package="200 mil [THT, electrolytic]"]
  D2 = Diode [package=diode-hv]
  D1 = Diode [package=diode-hv]

nets:
  N1: J3.pin1, C2.+, U1.IN, J8.pin1, J9.pin2, J13.pin2, R15.Pin_1, J50.pin2
  N2: J3.pin2, C2.-, C3.-, J5.pin2, J6.pin1, J7.pin1, J10.pin1, C4.-, J12.pin1, C5.-, J15.pin1, U2.E, J14.pin1, J16.pin1, J18.pin1, J19.pin1, J21.pin1, J22.pin1, J24.pin1, J25.pin1, J27.pin1, J28.pin1, J30.pin1, J31.pin1, J33.pin1, J34.pin1, J36.pin1, J37.pin1, J39.pin1, C6.-, J48.pin1, J49.pin1, C8.-
  N3: U1.ADJ, R1.Pin_1, U2.S, U2.A
  N4: U1.OUT, C3.+, J5.pin1, R1.Pin_0, J17.pin2, J20.pin2, J23.pin2, J26.pin2, J29.pin2, J32.pin2, J35.pin2, J38.pin2
  N5: J6.pin2, D1.A
  N6: J7.pin2, D2.A
  N7: J8.pin2, C6.+, C7.+, D2.C, D1.C
  N8: J9.pin1, J10.pin2, C4.+, R3.Pin_0
  N9: R3.Pin_1, J12.pin2
  N10: J13.pin1, R4.Pin_0, C5.+, J15.pin2
  N11: R4.Pin_1, J14.pin2
  N12: J16.pin2, R5.Pin_1
  N13: R5.Pin_0, J17.pin1, J18.pin2
  N14: R6.Pin_0, J20.pin1, J21.pin2
  N15: R6.Pin_1, J19.pin2
  N16: R7.Pin_0, J23.pin1, J24.pin2
  N17: R7.Pin_1, J22.pin2
  N18: R8.Pin_0, J26.pin1, J27.pin2
  N19: R8.Pin_1, J25.pin2
  N20: R9.Pin_0, J29.pin1, J30.pin2
  N21: R9.Pin_1, J28.pin2
  N22: R10.Pin_0, J32.pin1, J33.pin2
  N23: R10.Pin_1, J31.pin2
  N24: R11.Pin_0, J35.pin1, J36.pin2
  N25: R11.Pin_1, J34.pin2
  N26: R12.Pin_0, J38.pin1, J39.pin2
  N27: R12.Pin_1, J37.pin2
  N28: J40.pin1, J42.pin2
  N29: J40.pin2, R13.Pin_1
  N30: J41.pin1, R13.Pin_0, J42.pin1
  N31: J43.pin1, J44.pin2
  N32: J43.pin2, J44.pin1
  N33: R14.Pin_0, J45.pin1, J46.pin1
  N34: R14.Pin_1, J47.pin2
  N35: J45.pin2, J47.pin1
  N36: C7.-, R15.Pin_0
  N37: R16.Pin_0, J49.pin2, J50.pin1, C8.+
  N38: R16.Pin_1, J48.pin2

notes:
  +
  -
  Baterias em paralelo
  Switch geral do robo
  voltímetro
  switch dos motores
  saída dos motores
  regulador ajustável - LM31K
  Voltimetro
  LED
  switch do arduino
  saída do arduino
  Led
  switch 1
  switch 2
  switch 3
  switch 4
  switch 5
  switch 6
  switch 7
  switch 8
  saída 5V
  Botao
  Start
  Reset
  Saida Digital
  5V
  GND
  switch do raspberry
  saída do raspberry
  2200uF
  Equipe Droid - UnB - Painel - Bruce
  Robogames 2017
